// Logisim project ALU.circ as structural Verilog: 1 circuit, main circuit ALU
module ALU (
  input  [31:0] A,
  input  [31:0] in_2,
  input  [31:0] B,
  input  [4:0] Shift,
  input  CarryIn,
  input  [3:0] Codop,
  output [3:0] Flags,
  output [31:0] S
);

  wire f_C_AmBpCm1, f_C_ApB, f_C_ApBpC, f_C_Blshift, f_C_BmA, f_C_Brashift, f_C_Brshift, subtractor_5_bout;
  wire [4:0] negator_1_out, shift_t, subtractor_1_out, subtractor_2_out;
  wire [31:0] AandB, AmBpCm1, AorB, ApB_entree, ApBpC, AtstB_entree, AxB, AxorB, BandnA, Blshift, BmA_entree,
       Brashift, Brrshift, Brshift, multiplexer_3_out, nA, not_2_out, subtractor_3_out, ZmA;

  BitSelector #(.width(32)) bitselector_1 (.in(B), .out(f_C_Blshift), .sel(negator_1_out));
  Negator #(.width(5)) negator_1 (.in(shift_t), .out(negator_1_out));
  BitSelector #(.width(32)) bitselector_2 (.in(B), .out(f_C_Brshift), .sel(subtractor_1_out));
  Subtractor #(.width(5)) subtractor_1 (.a(shift_t), .b(5'b00001), .out(subtractor_1_out));  // open: bin, bout
  BitSelector #(.width(32)) bitselector_3 (.in(B), .out(f_C_Brashift), .sel(subtractor_2_out));
  Subtractor #(.width(5)) subtractor_2 (.a(shift_t), .b(5'b00001), .out(subtractor_2_out));  // open: bin, bout
  assign AandB = A & B;  // AND_Gate and_1, 32 bits wide
  assign AxorB = A ^ B;  // XOR_Gate xor_1, 32 bits wide
  Shifter #(.width(32)) shifter_1 (.in(B), .\dist (Shift), .out(Blshift));
  Shifter #(.shift("lr"), .width(32)) shifter_2 (.in(B), .\dist (Shift), .out(Brshift));
  Shifter #(.shift("ar"), .width(32)) shifter_3 (.in(B), .\dist (Shift), .out(Brashift));
  Adder #(.width(32)) adder_1 (.a(A), .b(B), .out(ApBpC), .cin(CarryIn), .cout(f_C_ApBpC));
  Subtractor #(.width(32)) subtractor_3 (.a(A), .b(B), .out(subtractor_3_out), .bin(CarryIn), .bout(f_C_AmBpCm1));
  Shifter #(.shift("rr"), .width(32)) shifter_4 (.in(B), .\dist (Shift), .out(Brrshift));
  assign AtstB_entree = A & B;  // AND_Gate and_2, 32 bits wide
  assign AmBpCm1 = ~subtractor_3_out;  // NOT_Gate not_1, 32 bits wide
  assign not_2_out = ~A;  // NOT_Gate not_2, 32 bits wide
  Multiplexer #(.select(4)) multiplexer_1 (
    .in0(1'b0), .in1(1'b0), .in2(f_C_Blshift), .in3(f_C_Brshift), .in4(f_C_Brashift), .in5(f_C_ApBpC),
    .in6(f_C_AmBpCm1), .in7(Flags[3]), .in8(1'b0), .in9(1'b0), .in10(f_C_BmA), .in11(f_C_ApB), .in12(1'b0),
    .in13(1'b0), .in14(1'b0), .in15(1'b0), .out(Flags[1]), .sel(Codop));
  Subtractor #(.width(32)) subtractor_4 (.a(in_2), .b(A), .out(ZmA));  // open: bin, bout
  Subtractor #(.width(32)) subtractor_5 (.a(B), .b(A), .out(BmA_entree), .bout(subtractor_5_bout));  // open: bin
  Adder #(.width(32)) adder_2 (.a(A), .b(B), .out(ApB_entree), .cout(f_C_ApB));  // open: cin
  Multiplier #(.width(32)) multiplier_1 (.a(A), .b(B), .out(AxB));  // open: cin, cout
  assign AorB = A | B;  // OR_Gate or_1, 32 bits wide
  assign BandnA = B & not_2_out;  // AND_Gate and_3, 32 bits wide
  assign nA = ~A;  // NOT_Gate not_3, 32 bits wide
  not not_4 (f_C_BmA, subtractor_5_bout);
  Multiplexer #(.select(4), .width(32)) multiplexer_2 (
    .in0(AandB), .in1(AxorB), .in2(Blshift), .in3(Brshift), .in4(Brashift), .in5(ApBpC), .in6(AmBpCm1),
    .in7(Brrshift), .in8(B), .in9(ZmA), .in10(B), .in11(B), .in12(AorB), .in13(AxB), .in14(BandnA),
    .in15(nA), .out(S), .sel(Codop));
  Multiplexer #(.select(4), .width(32)) multiplexer_3 (
    .in0(S), .in1(S), .in2(S), .in3(S), .in4(S), .in5(S), .in6(S), .in7(S), .in8(AtstB_entree), .in9(S),
    .in10(BmA_entree), .in11(ApB_entree), .in12(S), .in13(S), .in14(S), .in15(S), .out(multiplexer_3_out),
    .sel(Codop));
  Comparator #(.width(32)) comparator_1 (
    .a(multiplexer_3_out), .b({32{1'b0}}), .eq(Flags[2]), .lt(Flags[3]));  // open: gt

  // Other names for the same wires on the sheet: ApB[31:0] = B; AtstB[31:0] = B; BmA[31:0] = B; CI = CarryIn;
  //   Flag[3:0] = Flags; V = Flags[0]; C = Flags[1]; Z = Flags[2]; f_C_Brrshift = Flags[3]; N = Flags[3]
endmodule
